# Fritzing sketch schema (saved by Fritzing 0.8.5b)
breadboards: 1

parts:
  U1 = attiny85 [package=dip]  # not connected
  S1 = Pushbutton [package="[THT]"]
  R1 = Resistor [tolerance=±5% resistance=220 package=THT]
  R2 = Resistor [tolerance=±5% resistance=10k package=THT]
  R3 = PHOTOCELL [package=photocell-kit]  # not connected
  LED1 = smd LED [color="Green (560nm)" package="1206 [SMD]"]
  R4 = Resistor [tolerance=±5% resistance=330 package=THT]
  R5 = Resistor [tolerance=±5% resistance=10k package=THT]
  R6 = Resistor [tolerance=±5% resistance=220 package=THT]
  Power_plug1 = Power plug
  LED2 = smd LED [color="Red (633nm)" package="1206 [SMD]"]

nets:
  N1: S1.Pin_1, S1.Pin_2, R1.Pin_0
  N2: S1.Pin_3, S1.Pin_4, LED1.anode, Power_plug1.GND
  N3: R1.Pin_1, R2.Pin_1, R4.Pin_1, R5.Pin_0, Power_plug1.VCC, LED2.cathode
  N4: LED1.cathode, R4.Pin_0
  N5: R5.Pin_1, R6.Pin_0, LED2.anode
